// Logisim project processador rev1.circ as structural Verilog: 1 circuit, main circuit main
module main (
  input  [7:0] Input,
  input  Reset,
  output [7:0] out_3
);

  wire and_1_out, and_3_out, and_4_out, and_5_out, and_6_out, and_7_out, and_8_out, and_9_out, and_10_out,
       and_11_out, and_12_out, and_13_out, and_14_out, and_15_out, and_16_out, and_17_out, and_18_out,
       and_19_out, and_20_out, and_21_out, and_22_out, and_23_out, and_24_out, and_25_out, and_26_out,
       and_27_out, and_28_out, and_29_out, clock_1_out, d_ff_1_qn, d_ff_2_qn, d_ff_3_qn, d_ff_4_qn,
       d_ff_5_qn, d_ff_6_qn, d_ff_7_qn, d_ff_8_qn, d_ff_9_qn, d_ff_10_q, d_ff_10_qn, d_ff_11_q, d_ff_11_qn,
       d_ff_12_q, d_ff_12_qn, demultiplexer_1_out1, demultiplexer_1_out2, demultiplexer_1_out4,
       demultiplexer_1_out5, demultiplexer_1_out6, demultiplexer_1_out7, demultiplexer_1_out8, nor_1_out,
       nor_2_out, not_1_out, not_2_out, not_3_out, not_4_out, not_5_out, not_6_out, not_7_out, not_8_out,
       not_9_out, not_10_out, not_11_out, not_13_out, not_14_out, not_15_out, not_16_out, not_17_out,
       not_18_out, not_19_out, or_1_out, or_2_out, or_3_out, or_4_out, or_5_out, or_6_out, or_7_out,
       or_8_out, or_9_out, t_ff_1_qn, xor_1_out, xor_3_out, xor_5_out, xor_7_out;
  wire [3:0] adder_1_out, adder_2_out, register_1_q, register_2_q, register_3_q, rom_1_data, xor_2_out,
       xor_4_out;
  wire [3:3] and_2_out, not_12_out;
  wire [7:0] adder_3_out, adder_4_out, adder_5_out, d_ff_1_q, multiplexer_1_out, multiplexer_2_out,
       multiplexer_3_out, ram_1_data, ram_2_data, register_4_q, register_5_q, xor_6_out, xor_8_out;
  wire [7:7] demultiplexer_1_out0, demultiplexer_1_out3;

  not not_1 (not_1_out, rom_1_data[3]);
  and and_1 (and_1_out, not_1_out, rom_1_data[2], rom_1_data[1]);
  and and_2 (and_2_out[3], and_1_out, rom_1_data[0]);
  Clock #(.highDuration(1), .lowDuration(1)) clock_1 (.out(clock_1_out));
  xor xor_1 (xor_1_out, and_2_out[3], 1'b1);
  assign xor_2_out = {4{and_2_out[3]}} ^ 4'b0000;  // XOR_Gate xor_2, 4 bits wide
  D_Flip_Flop d_ff_1 (
    .clk(d_ff_3_qn), .D(d_ff_1_qn), .Q(d_ff_1_q[0]), .Qn(d_ff_1_qn), .preset(and_4_out), .reset(and_3_out));  // open: en
  and and_3 (and_3_out, or_3_out, not_2_out);
  and and_4 (and_4_out, multiplexer_1_out[0], or_3_out);
  not not_2 (not_2_out, multiplexer_1_out[0]);
  D_Flip_Flop d_ff_2 (
    .clk(d_ff_8_qn), .D(d_ff_2_qn), .Q(d_ff_1_q[4]), .Qn(d_ff_2_qn), .preset(and_6_out), .reset(and_5_out));  // open: en
  and and_5 (and_5_out, or_3_out, not_3_out);
  and and_6 (and_6_out, multiplexer_1_out[4], or_3_out);
  not not_3 (not_3_out, multiplexer_1_out[4]);
  and and_7 (and_7_out, and_1_out, xor_1_out);
  D_Flip_Flop d_ff_3 (.clk(or_2_out), .D(d_ff_3_qn), .Qn(d_ff_3_qn), .reset(Reset));  // open: Q, preset, en
  D_Flip_Flop d_ff_4 (
    .clk(d_ff_1_qn), .D(d_ff_4_qn), .Q(d_ff_1_q[1]), .Qn(d_ff_4_qn), .preset(and_9_out), .reset(and_8_out));  // open: en
  and and_8 (and_8_out, or_3_out, not_4_out);
  and and_9 (and_9_out, multiplexer_1_out[1], or_3_out);
  not not_4 (not_4_out, multiplexer_1_out[1]);
  D_Flip_Flop d_ff_5 (
    .clk(d_ff_2_qn), .D(d_ff_5_qn), .Q(d_ff_1_q[5]), .Qn(d_ff_5_qn), .preset(and_10_out), .reset(and_11_out));  // open: en
  and and_10 (and_10_out, multiplexer_1_out[5], or_3_out);
  and and_11 (and_11_out, or_3_out, not_5_out);
  not not_5 (not_5_out, multiplexer_1_out[5]);
  Adder #(.width(4)) adder_1 (.a(register_1_q), .b(xor_2_out), .out(adder_1_out), .cin(and_7_out));  // open: cout
  D_Flip_Flop d_ff_6 (
    .clk(d_ff_4_qn), .D(d_ff_6_qn), .Q(d_ff_1_q[2]), .Qn(d_ff_6_qn), .preset(and_13_out), .reset(and_12_out));  // open: en
  and and_12 (and_12_out, or_3_out, not_6_out);
  and and_13 (and_13_out, multiplexer_1_out[2], or_3_out);
  D_Flip_Flop d_ff_7 (
    .clk(d_ff_5_qn), .D(d_ff_7_qn), .Q(d_ff_1_q[6]), .Qn(d_ff_7_qn), .preset(and_15_out), .reset(and_14_out));  // open: en
  and and_14 (and_14_out, or_3_out, not_7_out);
  and and_15 (and_15_out, multiplexer_1_out[6], or_3_out);
  and and_16 (and_16_out, multiplexer_1_out[3], or_3_out);
  not not_6 (not_6_out, multiplexer_1_out[2]);
  and and_17 (and_17_out, multiplexer_1_out[7], or_3_out);
  not not_7 (not_7_out, multiplexer_1_out[6]);
  Register #(.width(4)) register_1 (.D(adder_1_out), .Q(register_1_q), .clk(d_ff_3_qn), .clr(and_25_out));  // open: en
  nor nor_1 (nor_1_out, register_1_q[3], register_1_q[2], register_1_q[1], register_1_q[0], 1'b0);
  and and_18 (and_18_out, nor_1_out, and_21_out);
  D_Flip_Flop d_ff_8 (
    .clk(d_ff_6_qn), .D(d_ff_8_qn), .Q(d_ff_1_q[3]), .Qn(d_ff_8_qn), .preset(and_16_out), .reset(and_19_out));  // open: en
  and and_19 (and_19_out, or_3_out, not_8_out);
  not not_8 (not_8_out, multiplexer_1_out[3]);
  D_Flip_Flop d_ff_9 (
    .clk(d_ff_7_qn), .D(d_ff_9_qn), .Q(d_ff_1_q[7]), .Qn(d_ff_9_qn), .preset(and_17_out), .reset(and_20_out));  // open: en
  and and_20 (and_20_out, or_3_out, not_9_out);
  not not_9 (not_9_out, multiplexer_1_out[7]);
  T_Flip_Flop t_ff_1 (.clk(clock_1_out), .T(and_25_out), .Qn(t_ff_1_qn), .reset(or_1_out));  // open: Q, preset, en
  or or_1 (or_1_out, and_18_out, Reset);
  not not_10 (not_10_out, t_ff_1_qn);
  and and_21 (and_21_out, not_10_out, and_22_out);
  and and_22 (and_22_out, register_2_q[2], register_2_q[1], register_2_q[0]);
  Register #(.width(4)) register_2 (.D(rom_1_data), .Q(register_2_q), .clk(d_ff_3_qn));  // open: en, clr
  Demultiplexer #(.select(4), .width(1), .tristate("false")) demultiplexer_1 (
    .out0(demultiplexer_1_out0[7]), .out1(demultiplexer_1_out1), .out2(demultiplexer_1_out2),
    .out3(demultiplexer_1_out3[7]), .out4(demultiplexer_1_out4), .out5(demultiplexer_1_out5),
    .out6(demultiplexer_1_out6), .out7(demultiplexer_1_out7), .out8(demultiplexer_1_out8), .in(t_ff_1_qn),
    .sel(rom_1_data));  // open: out9, out10, out11, out12, out13, out14, out15
  or or_2 (or_2_out, demultiplexer_1_out8, clock_1_out);
  ROM #(.addrWidth(8), .dataWidth(4)) rom_1 (.addr(d_ff_1_q), .data(rom_1_data));  // open: sel
  or or_3 (or_3_out, and_24_out, Reset);
  and and_23 (and_23_out, demultiplexer_1_out6, not_11_out);
  not not_11 (not_11_out, nor_2_out);
  not not_12 (not_12_out[3], demultiplexer_1_out6);
  not not_13 (not_13_out, nor_2_out);
  and and_24 (and_24_out, demultiplexer_1_out7, not_14_out);
  not not_14 (not_14_out, nor_2_out);
  and and_25 (and_25_out, demultiplexer_1_out6, nor_2_out);
  and and_26 (and_26_out, demultiplexer_1_out6, not_13_out);
  or or_4 (or_4_out, and_26_out, and_27_out);
  and and_27 (and_27_out, demultiplexer_1_out7, nor_2_out);
  or or_5 (or_5_out, demultiplexer_1_out0[7], demultiplexer_1_out1);
  or or_6 (or_6_out, 1'b0, demultiplexer_1_out5, demultiplexer_1_out1, demultiplexer_1_out4, demultiplexer_1_out0[7]);
  xor xor_3 (xor_3_out, not_12_out[3], 1'b1);
  assign xor_4_out = {4{not_12_out[3]}} ^ 4'b0000;  // XOR_Gate xor_4, 4 bits wide
  not not_15 (not_15_out, or_6_out);
  or or_7 (or_7_out, not_15_out, or_2_out);
  Multiplexer #(.select(1), .width(8)) multiplexer_1 (
    .in0(adder_4_out), .in1({8{1'b0}}), .out(multiplexer_1_out), .sel(Reset));
  xor xor_5 (xor_5_out, demultiplexer_1_out3[7], 1'b1);
  assign xor_6_out = {8{demultiplexer_1_out3[7]}} ^ {8{1'b0}};  // XOR_Gate xor_6, 8 bits wide
  not not_16 (not_16_out, d_ff_10_q);
  D_Flip_Flop d_ff_10 (
    .clk(or_7_out), .D(d_ff_10_qn), .Q(d_ff_10_q), .Qn(d_ff_10_qn), .reset(Reset));  // open: preset, en
  Adder #(.width(4)) adder_2 (.a(register_3_q), .b(xor_4_out), .out(adder_2_out), .cin(xor_3_out));  // open: cout
  and and_28 (and_28_out, d_ff_11_q, or_4_out);
  D_Flip_Flop d_ff_11 (.clk(or_2_out), .D(d_ff_11_qn), .Q(d_ff_11_q), .Qn(d_ff_11_qn));  // open: preset, en, reset
  or or_8 (or_8_out, demultiplexer_1_out3[7], demultiplexer_1_out2);
  RAM #(.addrWidth(8), .dataWidth(8)) ram_1 (
    .addr(register_4_q), .data(ram_1_data), .clk(or_7_out), .ld(not_16_out), .clr(Reset));  // open: sel
  nor nor_2 (nor_2_out, ram_1_data[7], ram_1_data[6], ram_1_data[5], ram_1_data[4], ram_1_data[3], ram_1_data[2], ram_1_data[1], ram_1_data[0], 1'b0);
  Register #(.width(4)) register_3 (.D(adder_2_out), .Q(register_3_q), .clk(and_28_out), .clr(Reset));  // open: en
  Adder #(.width(8)) adder_3 (.a(register_4_q), .b(xor_6_out), .out(adder_3_out), .cin(xor_5_out));  // open: cout
  not not_17 (not_17_out, or_8_out);
  or or_9 (or_9_out, not_17_out, or_2_out);
  assign ram_1_data = d_ff_10_q ? multiplexer_2_out : 8'bz;  // Controlled_Buffer controlled_buffer_1
  Adder #(.width(8)) adder_4 (.a(ram_2_data), .b({8{1'b0}}), .out(adder_4_out), .cin(1'b1));  // open: cout
  Register #(.width(8)) register_4 (.D(adder_3_out), .Q(register_4_q), .clk(d_ff_12_q), .clr(Reset));  // open: en
  D_Flip_Flop d_ff_12 (
    .clk(or_9_out), .D(d_ff_12_qn), .Q(d_ff_12_q), .Qn(d_ff_12_qn), .reset(Reset));  // open: preset, en
  not not_18 (not_18_out, d_ff_11_q);
  Multiplexer #(.select(1), .width(8)) multiplexer_2 (
    .in0(multiplexer_3_out), .in1(adder_5_out), .out(multiplexer_2_out), .sel(or_5_out));
  Register #(.width(8)) register_5 (.D(ram_1_data), .Q(register_5_q), .clk(or_7_out), .clr(Reset));  // open: en
  xor xor_7 (xor_7_out, demultiplexer_1_out0[7], 1'b1);
  assign xor_8_out = {8{demultiplexer_1_out0[7]}} ^ {8{1'b0}};  // XOR_Gate xor_8, 8 bits wide
  RAM #(.addrWidth(4), .dataWidth(8)) ram_2 (
    .addr(register_3_q), .data(ram_2_data), .clk(not_18_out), .ld(not_19_out), .clr(Reset));  // open: sel
  not not_19 (not_19_out, and_23_out);
  Adder #(.width(8)) adder_5 (.a(xor_8_out), .b(register_5_q), .out(adder_5_out), .cin(xor_7_out));  // open: cout
  assign ram_2_data = and_23_out ? d_ff_1_q : 8'bz;  // Controlled_Buffer controlled_buffer_2
  Multiplexer #(.select(1), .width(8)) multiplexer_3 (
    .in0(Input), .in1(out_3), .out(multiplexer_3_out), .sel(demultiplexer_1_out5));
  Register #(.width(8)) register_6 (.D(ram_1_data), .Q(out_3), .clk(and_29_out), .clr(Reset));  // open: en
  and and_29 (and_29_out, or_7_out, demultiplexer_1_out5);

  // Notes on the sheet:
  //   Clock
  //   2-pulses instruction cycle
  //   Program Counter Register
  //   Bracket Counter
  //   8-bit Adress Bus
  //   Harvard Brain Fuck Processor
  //   HBF-4080
  //   4-bit Command Bus
  //   Halt
  //   256-Word Program Memory
  //   contents of rom_1 (hex, n*v repeats v):
  //   4 6 6 0 2 1 1 3 7 9 7 9 2 5 8
  //   Program Flux Control Unit
  //   Pointer Manipulation Unit
  //   256-Bytes Data Memory
  //   Stack Pointer Register
  //   Zero Status Flag
  //   8-bit Data Bus
  //   Work Register
  //   16-Levels Stack
  //   Logic Arithmeticl Unit
  //   Command set OpCodes
  //   +                        0
  //   -                         1
  //   >                         2
  //   <                          3
  //   .                           4
  //   ,                           5
  //   [                            6
  //   ]                            7
  //   END                      8
  //   ~            Any Other
  //   Output
endmodule
